# Fritzing sketch Book Project (saved by Fritzing 0.9.3b)
circuit board: 8.46667cm x 5.64444cm
breadboards: 1

parts:
  U1 = atmega328 [package=dip]
  U2 = microSD Socket [package=micro-sd-socket-pp]
  Micro_SD = Header 6 [package=molex-1x6-ra]
  part = Resistor [tolerance=±5% resistance=10k package=THT]
  part_2 = Resistor [tolerance=±5% resistance=10k package=THT]
  part_3 = Resistor [tolerance=±5% resistance=10k package=THT]
  Sensor_1 = molex pin header, 2 pins [form=molex]
  Sensor_2 = molex pin header, 2 pins [form=molex]
  Sensor_3 = molex pin header, 2 pins [form=molex]
  Power = molex pin header, 2 pins [form=molex]
  Sensor_4 = molex pin header, 2 pins [form=molex]
  R2 = Resistor [tolerance=±5% resistance=10k package=THT]
  Speaker = molex pin header, 2 pins [form=molex]

nets:
  VCC: U1.VCC, U2.VCC, Micro_SD.3, Power.pin1
  GND: U1.GND, U2.GND, Micro_SD.5, part.Pin_0, part_2.Pin_0, part_3.Pin_0, Power.pin2, R2.Pin_0, Speaker.pin2
  N1: U1.XLAT2, U2.CS, Micro_SD.1
  N2: U1.D5_(PWM), U2.DI, Micro_SD.2
  N3: U1.D6_(PWM), U2.DO, Micro_SD.6
  N4: U1.D7, U2.SCK, Micro_SD.4
  N5: part.Pin_1, Sensor_2.pin1
  N6: part_2.Pin_1, Sensor_3.pin1
  N7: part_3.Pin_1, Sensor_1.pin1
  N8: Sensor_4.pin1, R2.Pin_1
