# Fritzing sketch NaniteSMD (saved by Fritzing 0.8.7b)
circuit board: 3.80059cm x 1.30762cm
breadboards: 1

parts:
  3_6v = DIODE-ZENER [package=diode-zener]
  3_6v_2 = DIODE-ZENER [package=diode-zener]
  USB_MiniB = USB Connectors [package=usb-minib-nostop]
  Tiny85 = ATTINY13 [package=so]
  S1 = Momentary Switch [package=tactile_switch_smd]
  part = attiny85 [package=dip]
  LED1 = smd LED [color="Red (633nm)" package="0805 [SMD]"]
  R4 = Resistor [tolerance=±0.05% resistance=68 package="0805 [SMD]"]
  R2 = Resistor [tolerance=±5% resistance=220 package="0805 [SMD]"]
  R1 = Resistor [tolerance=±5% resistance=10k package="0805 [SMD]"]
  R3 = Resistor [tolerance=±0.05% resistance=2.2k package="0805 [SMD]"]

nets:
  N1: 3_6v.C, USB_MiniB.D-, R4.Pin_0, R1.Pin_0
  GND: 3_6v.A, 3_6v_2.A, USB_MiniB.GND, Tiny85.GND, S1.3, part.Pin_4
  N2: 3_6v_2.C, USB_MiniB.D+, R3.Pin_0
  5V: USB_MiniB.VBUS, Tiny85.VCC, part.Pin_8, R2.Pin_0, R1.Pin_1
  N3: Tiny85.PB5(NRES), S1.1, part.Pin_1, LED1.cathode
  N4: Tiny85.PB3(ADC3), part.Pin_3, R4.Pin_1
  N5: Tiny85.PB4(ADC2), part.Pin_2, R3.Pin_1
  N6: Tiny85.PB0(MOSI), part.Pin_5
  N7: Tiny85.PB1(MISO), part.Pin_6
  N8: Tiny85.PB2(SCK_ADC1), part.Pin_7
  N9: LED1.anode, R2.Pin_1

notes:
  WhileyLabs
